# Fritzing sketch IoT_nuclear_radiation_sensor (saved by Fritzing 0.9.10b)

parts:
  WeMos_D1_Mini2 = WeMos D1 Mini
  R1 = Rotary Potentiometer (Small) [maximum_resistance=47kΩ knob_status=50% power=0.5W package=THT]

nets:
  N1: WeMos_D1_Mini2.A0, R1.leg1, R1.wiper
